// Logisim project calculator_asm.circ as structural Verilog: 1 circuit, main circuit main
module main (
  input  [3:0] X,
  input  [3:0] Y,
  input  [1:0] OP,
  input  Start,
  output Overflow,
  output Carry_Out
);

  wire adder_1_cout, and_1_out, and_2_out, and_3_out, and_4_out, and_5_out, clock_1_out, decoder_1_out0,
       decoder_1_out1, decoder_1_out2, decoder_1_out3, decoder_1_out6, not_1_out, or_1_out, or_2_out,
       or_3_out, or_4_out, xnor_1_out, xor_1_out, xor_2_out;
  wire [1:0] decoder_1_out4, or_6_out, RegOP_q;
  wire [2:0] d_ff_3_q;
  wire [3:0] adder_1_out, controlled_buffer_1_out, multiplexer_1_out, multiplexer_2_out, negator_1_out,
       negator_2_out, RegResult_q, RegX_q, RegY_q, shifter_1_out, shifter_2_out, shifter_3_out, shifter_4_out;

  Clock clock_1 (.out(clock_1_out));
  not not_1 (not_1_out, RegOP_q[1]);
  and and_1 (and_1_out, RegOP_q[1], decoder_1_out1);
  xor xor_1 (xor_1_out, d_ff_3_q[2], d_ff_3_q[1]);
  or or_1 (or_1_out, xor_1_out, and_2_out);
  and and_2 (and_2_out, decoder_1_out1, not_1_out);
  and and_3 (and_3_out, RegOP_q[0], decoder_1_out1);
  and and_4 (and_4_out, Start, decoder_1_out0);
  Register #(.width(4)) RegX (.D(X), .en(decoder_1_out1), .clk(clock_1_out), .Q(RegX_q));  // open: clr
  Register #(.width(4)) RegY (.D(Y), .en(decoder_1_out1), .clk(clock_1_out), .Q(RegY_q));  // open: clr
  Register #(.width(2)) RegOP (.D(OP), .en(decoder_1_out1), .clk(clock_1_out), .Q(RegOP_q));  // open: clr
  or or_2 (or_2_out, and_1_out, xor_1_out);
  or or_3 (or_3_out, and_3_out, and_4_out);
  D_Flip_Flop d_ff_1 (.D(or_2_out), .clk(clock_1_out), .Q(d_ff_3_q[2]));  // open: Qn, preset, reset
  D_Flip_Flop d_ff_2 (.D(or_1_out), .clk(clock_1_out), .Q(d_ff_3_q[1]));  // open: Qn, preset, reset
  D_Flip_Flop d_ff_3 (.D(or_3_out), .clk(clock_1_out), .Q(d_ff_3_q[0]));  // open: Qn, preset, reset
  Shifter #(.width(4)) shifter_1 (.in(RegX_q), .\dist (2'b01), .out(shifter_1_out));
  Shifter #(.shift("ar"), .width(4)) shifter_2 (.in(RegX_q), .\dist (2'b01), .out(shifter_2_out));
  Shifter #(.shift("ar"), .width(4)) shifter_3 (.in(RegY_q), .\dist (2'b01), .out(shifter_3_out));
  Shifter #(.width(4)) shifter_4 (.in(RegY_q), .\dist (2'b01), .out(shifter_4_out));
  Negator #(.width(4)) negator_1 (.in(RegY_q), .out(negator_1_out));
  Negator #(.width(4)) negator_2 (.in(shifter_4_out), .out(negator_2_out));
  Decoder #(.select(3)) decoder_1 (
    .out0(decoder_1_out0), .out1(decoder_1_out1), .out2(decoder_1_out2), .out3(decoder_1_out3),
    .out4(decoder_1_out4[0]), .out5(decoder_1_out4[1]), .out6(decoder_1_out6), .sel(d_ff_3_q));  // open: out7, en
  Multiplexer #(.select(2), .width(4)) multiplexer_1 (
    .in0(RegX_q), .in1(shifter_1_out), .in2(shifter_2_out), .out(multiplexer_1_out), .sel(decoder_1_out4));  // open: in3
  Multiplexer #(.select(2), .width(4)) multiplexer_2 (
    .in0(RegY_q), .in1(negator_1_out), .in2(shifter_3_out), .in3(negator_2_out), .out(multiplexer_2_out),
    .sel(or_6_out));
  or or_4 (or_4_out, decoder_1_out2, decoder_1_out3, decoder_1_out4[0], decoder_1_out4[1]);
  or or_5 (or_6_out[1], decoder_1_out4[0], decoder_1_out4[1]);
  or or_6 (or_6_out[0], decoder_1_out3, decoder_1_out4[1]);
  Adder #(.width(4)) adder_1 (
    .a(multiplexer_1_out), .b(multiplexer_2_out), .out(adder_1_out), .cout(adder_1_cout));  // open: cin
  Register #(.width(4)) RegResult (.D(adder_1_out), .en(or_4_out), .clk(clock_1_out), .Q(RegResult_q));  // open: clr
  Register #(.width(1)) register_1 (.D(adder_1_cout), .en(or_4_out), .clk(clock_1_out), .Q(Carry_Out));  // open: clr
  xnor xnor_1 (xnor_1_out, multiplexer_1_out[3], multiplexer_2_out[3]);
  xor xor_2 (xor_2_out, multiplexer_1_out[3], adder_1_out[3]);
  assign controlled_buffer_1_out = decoder_1_out6 ? RegResult_q : 4'bz;  // Controlled_Buffer controlled_buffer_1
  Register #(.width(1)) register_2 (.D(and_5_out), .en(or_4_out), .clk(clock_1_out), .Q(Overflow));  // open: clr
  and and_5 (and_5_out, xnor_1_out, xor_2_out);
  Hex_Digit_Display hex_digit_display_1 (.value(controlled_buffer_1_out));  // open: dp
endmodule
