// Logisim project circuit_design.circ as structural Verilog
module Q1 (
  input  A,
  input  B,
  input  C,
  input  D,
  output F
);

  wire and_1_out, and_2_out, and_3_out, and_4_out, not_1_out, not_2_out, not_3_out, not_4_out;

  not not_1 (not_1_out, A);
  not not_2 (not_2_out, B);
  not not_3 (not_3_out, C);
  not not_4 (not_4_out, D);
  and and_1 (and_1_out, not_2_out, not_4_out);
  and and_2 (and_2_out, not_1_out, not_3_out, not_4_out);
  and and_3 (and_3_out, B, C, D);
  and and_4 (and_4_out, A, B, D);
  or or_1 (F, and_1_out, and_2_out, and_3_out, and_4_out);
endmodule

module Q2a (
  input  A,
  input  B,
  input  C,
  input  D,
  output F
);

  wire and_1_out, and_2_out, and_3_out, and_4_out, not_1_out, not_2_out, not_3_out;

  not not_1 (not_1_out, B);
  not not_2 (not_2_out, C);
  not not_3 (not_3_out, D);
  and and_1 (and_1_out, A, C, not_3_out);
  and and_2 (and_2_out, not_2_out, D);
  and and_3 (and_3_out, A, not_1_out);
  and and_4 (and_4_out, A, B, C, D);
  or or_1 (F, and_1_out, and_2_out, and_3_out, and_4_out);
endmodule

module Q2b (
  input  A,
  input  B,
  input  C,
  input  D,
  output F
);

  wire not_1_out, not_2_out, not_3_out, not_4_out, or_1_out, or_2_out, or_3_out, or_4_out;

  not not_1 (not_1_out, A);
  not not_2 (not_2_out, B);
  not not_3 (not_3_out, C);
  not not_4 (not_4_out, D);
  or or_1 (or_1_out, not_1_out, B, not_4_out);
  or or_2 (or_2_out, not_2_out, not_1_out, not_3_out);
  or or_3 (or_3_out, not_1_out, not_2_out, C);
  or or_4 (or_4_out, not_2_out, C, not_4_out);
  and and_1 (F, or_1_out, or_2_out, or_3_out, or_4_out);
endmodule

module Q3_NOR (
  input  A,
  input  B,
  input  C,
  input  D,
  output G
);

  wire nor_1_out, nor_2_out, nor_3_out, not_1_out;

  not not_1 (not_1_out, D);
  nor nor_1 (nor_1_out, A, B);
  nor nor_2 (nor_2_out, A, C);
  nor nor_3 (nor_3_out, B, C);
  nor nor_4 (G, nor_1_out, nor_2_out, nor_3_out, not_1_out);
endmodule

module Q3_NAND (
  input  A,
  input  B,
  input  C,
  input  D,
  output F,
  output G
);

  wire nand_1_out, nand_2_out, nand_3_out, nor_1_out, nor_2_out, nor_3_out, nor_4_out, not_1_out, not_2_out,
       not_3_out, not_4_out;

  not not_1 (not_1_out, A);
  not not_2 (not_2_out, B);
  not not_3 (not_3_out, C);
  not not_4 (not_4_out, D);
  nand nand_1 (nand_1_out, B, C, D);
  nand nand_2 (nand_2_out, A, C, D);
  nand nand_3 (nand_3_out, A, B, D);
  nor nor_1 (nor_1_out, not_2_out, not_3_out, not_4_out);
  nor nor_2 (nor_2_out, not_1_out, not_3_out, not_4_out);
  nor nor_3 (nor_3_out, not_1_out, not_2_out, not_4_out);
  nand nand_4 (F, nand_1_out, nand_2_out, nand_3_out);
  nor nor_4 (nor_4_out, nor_1_out, nor_2_out, nor_3_out);
  not not_5 (G, nor_4_out);
endmodule

module Design_Problem (
  input  A,
  input  B,
  input  C,
  input  D,
  output X,
  output Y
);

  wire and_1_out, and_2_out, and_3_out, and_4_out, and_5_out, and_6_out, not_1_out, not_2_out, not_3_out,
       not_4_out;

  not not_1 (not_1_out, A);
  not not_2 (not_2_out, B);
  not not_3 (not_3_out, C);
  not not_4 (not_4_out, D);
  and and_1 (and_1_out, not_1_out, not_2_out, C);
  and and_2 (and_2_out, not_1_out, C, D);
  and and_3 (and_3_out, A, not_3_out, not_4_out);
  and and_4 (and_4_out, A, B, not_3_out);
  and and_5 (and_5_out, not_2_out, D);
  and and_6 (and_6_out, B, not_4_out);
  or or_1 (X, and_1_out, and_2_out, and_3_out, and_4_out);
  or or_2 (Y, and_5_out, and_6_out);
endmodule

module Q3 (
  input  A,
  input  B,
  input  C,
  input  D,
  output F,
  output G
);

  wire and_1_out, and_2_out, and_3_out, nand_1_out, nand_2_out, nand_3_out;

  nand nand_1 (nand_1_out, B, C, D);
  nand nand_2 (nand_2_out, A, C, D);
  nand nand_3 (nand_3_out, A, B, D);
  and and_1 (and_1_out, B, C, D);
  and and_2 (and_2_out, A, C, D);
  and and_3 (and_3_out, A, B, D);
  nand nand_4 (F, nand_1_out, nand_2_out, nand_3_out);
  or or_1 (G, and_1_out, and_2_out, and_3_out);
endmodule
