// Logisim project sequence_detector.circ as structural Verilog: 1 circuit, main circuit main
module main (
  input  X,
  output Z1,
  output Z0
);

  wire clock_1_out, nand_1_out, nand_2_out, nand_4_out, nand_5_out, nand_6_out, nand_7_out, nand_8_out, Q0_q,
       Q0_qn, Q1_q, Q1_qn;

  nand nand_1 (nand_1_out, X, X);
  nand nand_2 (nand_2_out, Q0_q, Q1_q);
  nand nand_3 (Z1, nand_2_out, nand_2_out);
  nand nand_4 (nand_4_out, Q0_qn, Q1_q, nand_1_out);
  nand nand_5 (nand_5_out, Q0_q, Q1_qn, X);
  nand nand_6 (nand_6_out, Q0_qn, Q1_q, X);
  nand nand_7 (nand_7_out, nand_4_out, nand_5_out);
  nand nand_8 (nand_8_out, nand_6_out, nand_6_out);
  D_Flip_Flop Q0 (.D(nand_1_out), .clk(clock_1_out), .Q(Q0_q), .Qn(Q0_qn));  // open: preset, reset
  D_Flip_Flop Q1 (.D(nand_7_out), .clk(clock_1_out), .Q(Q1_q), .Qn(Q1_qn));  // open: preset, reset
  D_Flip_Flop Q2 (.D(nand_8_out), .clk(clock_1_out), .Q(Z0));  // open: Qn, preset, reset
  Clock clock_1 (.out(clock_1_out));
endmodule
